// Logisim project ALU2.circ as structural Verilog: 9 circuits, main circuit main
module main (
  input  [15:0] InputA,
  input  [15:0] InputB,
  input  [2:0] Control_Input,
  output [15:0] Output,
  output Zero,
  output Sign,
  output Carry,
  output Overflow
);

  wire [3:0] addercircuit_1_zero, subtractorcircuit_1_zero;
  wire [15:0] addercircuit_1_y, bitwiseand_1_y, bitwisenot_1_y, bitwiseor_1_y, bitwisexor_1_y, shiftleft_1_y,
       shiftright_1_y, subtractorcircuit_1_y;

  Hex_Digit_Display hex_digit_display_1 (.value(InputA[15:12]));  // open: dp
  Hex_Digit_Display hex_digit_display_2 (.value(InputA[11:8]));  // open: dp
  Hex_Digit_Display hex_digit_display_3 (.value(InputB[15:12]));  // open: dp
  Hex_Digit_Display hex_digit_display_4 (.value(InputB[11:8]));  // open: dp
  Hex_Digit_Display hex_digit_display_5 (.value(InputA[7:4]));  // open: dp
  Hex_Digit_Display hex_digit_display_6 (.value(InputA[3:0]));  // open: dp
  Hex_Digit_Display hex_digit_display_7 (.value(InputB[7:4]));  // open: dp
  Hex_Digit_Display hex_digit_display_8 (.value(InputB[3:0]));  // open: dp
  BitWiseAnd bitwiseand_1 (.A(InputA), .B(InputB), .Y(bitwiseand_1_y));
  BitWiseOR bitwiseor_1 (.A(InputA), .B(InputB), .Y(bitwiseor_1_y));
  BitWiseNot bitwisenot_1 (.A(InputA), .Y(bitwisenot_1_y));
  BitWiseXOR bitwisexor_1 (.A(InputA), .B(InputB), .Y(bitwisexor_1_y));
  ShiftLeft shiftleft_1 (.A(InputA), .B(InputB), .Y(shiftleft_1_y));
  ShiftRight shiftright_1 (.A(InputA), .B(InputB), .Y(shiftright_1_y));
  AdderCircuit addercircuit_1 (
    .A(InputA), .B(InputB), .Zero(addercircuit_1_zero[0]), .Sign(addercircuit_1_zero[1]),
    .Carry(addercircuit_1_zero[2]), .Overflow(addercircuit_1_zero[3]), .Y(addercircuit_1_y));
  SubtractorCircuit subtractorcircuit_1 (
    .A(InputA), .B(InputB), .Y(subtractorcircuit_1_y), .Zero(subtractorcircuit_1_zero[0]),
    .Sign(subtractorcircuit_1_zero[1]), .Carry(subtractorcircuit_1_zero[2]),
    .Overflow(subtractorcircuit_1_zero[3]));
  Hex_Digit_Display hex_digit_display_9 (.value(Output[15:12]));  // open: dp
  Multiplexer #(.select(3), .width(16)) multiplexer_1 (
    .in0(addercircuit_1_y), .in1(subtractorcircuit_1_y), .in2(bitwiseand_1_y), .in3(bitwiseor_1_y),
    .in4(bitwisenot_1_y), .in5(bitwisexor_1_y), .in6(shiftleft_1_y), .in7(shiftright_1_y), .out(Output),
    .sel(Control_Input));
  Hex_Digit_Display hex_digit_display_10 (.value(Output[11:8]));  // open: dp
  Multiplexer #(.width(4)) multiplexer_2 (
    .in0(addercircuit_1_zero), .in1(subtractorcircuit_1_zero), .out({Overflow, Carry, Sign, Zero}),
    .sel(Control_Input[0]));
  Hex_Digit_Display hex_digit_display_11 (.value(Output[7:4]));  // open: dp
  Hex_Digit_Display hex_digit_display_12 (.value(Output[3:0]));  // open: dp
  LED led_1 (.in(Zero));
  LED led_2 (.in(Sign));
  LED led_3 (.in(Carry));
  LED led_4 (.in(Overflow));
endmodule

module BitWiseAnd (
  input  [15:0] A,
  input  [15:0] B,
  output [15:0] Y
);

  Hex_Digit_Display hex_digit_display_1 (.value(Y[15:12]));  // open: dp
  assign Y = A & B;  // AND_Gate and_1, 16 bits wide
  Hex_Digit_Display hex_digit_display_2 (.value(Y[11:8]));  // open: dp
  Hex_Digit_Display hex_digit_display_3 (.value(Y[7:4]));  // open: dp
  Hex_Digit_Display hex_digit_display_4 (.value(Y[3:0]));  // open: dp
  // LedBar #(.inputtype("row"), .matrixcols(16)) ledbar_1: pin names not known; wires that end beside it: Y

  // Notes on the sheet:
  //   Bit Wise AND
endmodule

module BitWiseOR (
  input  [15:0] A,
  input  [15:0] B,
  output [15:0] Y
);

  assign Y = A | B;  // OR_Gate or_1, 16 bits wide
  Hex_Digit_Display hex_digit_display_1 (.value(Y[15:12]));  // open: dp
  Hex_Digit_Display hex_digit_display_2 (.value(Y[11:8]));  // open: dp
  Hex_Digit_Display hex_digit_display_3 (.value(Y[7:4]));  // open: dp
  Hex_Digit_Display hex_digit_display_4 (.value(Y[3:0]));  // open: dp
  // LedBar #(.inputtype("row"), .matrixcols(16)) ledbar_1: pin names not known; wires that end beside it: Y

  // Notes on the sheet:
  //   Bit Wise OR
endmodule

module BitWiseNot (
  input  [15:0] A,
  output [15:0] Y
);

  assign Y = ~A;  // NOT_Gate not_1, 16 bits wide
  Hex_Digit_Display hex_digit_display_1 (.value(Y[15:12]));  // open: dp
  Hex_Digit_Display hex_digit_display_2 (.value(Y[11:8]));  // open: dp
  Hex_Digit_Display hex_digit_display_3 (.value(Y[7:4]));  // open: dp
  Hex_Digit_Display hex_digit_display_4 (.value(Y[3:0]));  // open: dp
  // LedBar #(.inputtype("row"), .matrixcols(16)) ledbar_1: pin names not known; wires that end beside it: Y

  // Notes on the sheet:
  //   Bit Wise NOT
endmodule

module BitWiseXOR (
  input  [15:0] A,
  input  [15:0] B,
  output [15:0] Y
);

  assign Y = A ^ B;  // XOR_Gate xor_1, 16 bits wide
  Hex_Digit_Display hex_digit_display_1 (.value(Y[15:12]));  // open: dp
  Hex_Digit_Display hex_digit_display_2 (.value(Y[11:8]));  // open: dp
  Hex_Digit_Display hex_digit_display_3 (.value(Y[7:4]));  // open: dp
  Hex_Digit_Display hex_digit_display_4 (.value(Y[3:0]));  // open: dp
  // LedBar #(.inputtype("row"), .matrixcols(16)) ledbar_1: pin names not known; wires that end beside it: Y

  // Notes on the sheet:
  //   16 BIT XOR
endmodule

module ShiftLeft (
  input  [15:0] A,
  input  [15:0] B,
  output [15:0] Y
);

  wire [3:0] bit_extender_1_out;

  Shifter #(.width(16)) shifter_1 (.in(A), .\dist (bit_extender_1_out), .out(Y));
  Bit_Extender #(.in_width(16), .out_width(4), .\type ("zero")) bit_extender_1 (.in(B), .out(bit_extender_1_out));
  Hex_Digit_Display hex_digit_display_1 (.value(Y[15:12]));  // open: dp
  Hex_Digit_Display hex_digit_display_2 (.value(Y[11:8]));  // open: dp
  Hex_Digit_Display hex_digit_display_3 (.value(Y[7:4]));  // open: dp
  Hex_Digit_Display hex_digit_display_4 (.value(Y[3:0]));  // open: dp
  // LedBar #(.inputtype("row"), .matrixcols(16)) ledbar_1: pin names not known; wires that end beside it: Y

  // Notes on the sheet:
  //   Shift A Left by B bits
endmodule

module ShiftRight (
  input  [15:0] A,
  input  [15:0] B,
  output [15:0] Y
);

  wire [3:0] bit_extender_1_out;

  Hex_Digit_Display hex_digit_display_1 (.value(Y[15:12]));  // open: dp
  Shifter #(.shift("lr"), .width(16)) shifter_1 (.in(A), .\dist (bit_extender_1_out), .out(Y));
  Bit_Extender #(.in_width(16), .out_width(4), .\type ("zero")) bit_extender_1 (.in(B), .out(bit_extender_1_out));
  Hex_Digit_Display hex_digit_display_2 (.value(Y[11:8]));  // open: dp
  Hex_Digit_Display hex_digit_display_3 (.value(Y[7:4]));  // open: dp
  Hex_Digit_Display hex_digit_display_4 (.value(Y[3:0]));  // open: dp
  // LedBar #(.inputtype("row"), .matrixcols(16)) ledbar_1: pin names not known; wires that end beside it: Y

  // Notes on the sheet:
  //   Shift Right A by B bits
endmodule

module AdderCircuit (
  input  [15:0] A,
  input  [15:0] B,
  output [15:0] Y,
  output Zero,
  output Sign,
  output Carry,
  output Overflow
);

  wire not_1_out;

  Adder #(.width(16)) adder_1 (.a(A), .b(B), .out({Sign, Y[14:0]}), .cout(Carry));  // open: cin
  Hex_Digit_Display hex_digit_display_1 (.value({Sign, Y[14:12]}));  // open: dp
  Hex_Digit_Display hex_digit_display_2 (.value(Y[11:8]));  // open: dp
  Hex_Digit_Display hex_digit_display_3 (.value(Y[7:4]));  // open: dp
  Hex_Digit_Display hex_digit_display_4 (.value(Y[3:0]));  // open: dp
  // LedBar #(.inputtype("row"), .matrixcols(16)) ledbar_1: pin names not known; wires that end beside it: {Sign, Y[14:0]}
  not not_1 (not_1_out, Sign);
  nor nor_1 (Zero, Y[0], Y[1], Y[2], Y[3], Y[4], Y[5], Y[6], Y[7], Y[8], Y[9], Y[10], Y[11], Y[12], Y[13], Y[14], Sign);
  and and_1 (Overflow, not_1_out, A[15], B[15]);
  LED led_1 (.in(Zero));
  LED led_2 (.in(Sign));
  LED led_3 (.in(Carry));
  LED led_4 (.in(Overflow));

  assign Y[15] = Sign;

  // Notes on the sheet:
  //   16 bit Adder Circuit
endmodule

module SubtractorCircuit (
  input  [15:0] A,
  input  [15:0] B,
  output [15:0] Y,
  output Zero,
  output Sign,
  output Carry,
  output Overflow
);

  wire not_1_out;

  Subtractor #(.width(16)) subtractor_1 (.a(A), .b(B), .out({Sign, Y[14:0]}), .bout(Carry));  // open: bin
  Hex_Digit_Display hex_digit_display_1 (.value({Sign, Y[14:12]}));  // open: dp
  Hex_Digit_Display hex_digit_display_2 (.value(Y[11:8]));  // open: dp
  Hex_Digit_Display hex_digit_display_3 (.value(Y[7:4]));  // open: dp
  Hex_Digit_Display hex_digit_display_4 (.value(Y[3:0]));  // open: dp
  not not_1 (not_1_out, Sign);
  // LedBar #(.inputtype("row"), .matrixcols(16)) ledbar_1: pin names not known; wires that end beside it: {Sign, Y[14:0]}
  nor nor_1 (Zero, Y[0], Y[1], Y[2], Y[3], Y[4], Y[5], Y[6], Y[7], Y[8], Y[9], Y[10], Y[11], Y[12], Y[13], Y[14], Sign);
  and and_1 (Overflow, not_1_out, A[15], ~B[15]);  // AND_Gate
  LED led_1 (.in(Zero));
  LED led_2 (.in(Sign));
  LED led_3 (.in(Carry));
  LED led_4 (.in(Overflow));

  assign Y[15] = Sign;

  // Notes on the sheet:
  //   16 bit Subtractor Circuit
endmodule
