// Logisim project SOLOMON EWUSI LAB 3 - ALU.circ as structural Verilog: 9 circuits, main circuit  Main ALU Circuit
module _16_Bit_AND (
  input  [15:0] A,
  input  [15:0] B,
  output [15:0] out_3
);

  assign out_3 = A & B;  // AND_Gate and_1, 16 bits wide

  // Notes on the sheet:
  //   16-Bit AND
endmodule

module _16_Bit_OR (
  input  [15:0] A,
  input  [15:0] B,
  output [15:0] Result
);

  assign Result = A | B;  // OR_Gate or_1, 16 bits wide

  // Notes on the sheet:
  //   16-Bit OR
endmodule

module _16_Bit_XOR (
  input  [15:0] A,
  input  [15:0] B,
  output [15:0] Result
);

  assign Result = A ^ B;  // XOR_Gate xor_1, 16 bits wide

  // Notes on the sheet:
  //   16-bit XOR
endmodule

module _16_Bit_Inverter (
  input  [15:0] A,
  output [15:0] Result
);

  assign Result = ~A;  // NOT_Gate not_1, 16 bits wide

  // Notes on the sheet:
  //   16-Bit Inverter
endmodule

module _16_Bit_Adder (
  input  [15:0] A,
  input  [15:0] B,
  output [15:0] Result,
  output Carry_Out,
  output Negative_Bit,
  output Zero_Bit,
  output Overflow_Bit
);

  wire and_1_out, and_2_out, not_2_out, not_3_out, not_4_out, or_1_out, xor_1_out, xor_2_out;

  Adder #(.width(16)) adder_1 (.a(A), .b(B), .out({Negative_Bit, Result[14:0]}), .cin(1'b0), .cout(Carry_Out));
  or or_1 (or_1_out, Negative_Bit, Result[14], Result[13], Result[12], Result[11], Result[10], Result[9], Result[8], Result[6], Result[5], Result[4], Result[3], Result[2], Result[1], Result[0], Result[7]);
  not not_1 (Zero_Bit, or_1_out);
  not not_2 (not_2_out, Negative_Bit);
  xor xor_1 (xor_1_out, Result[0], B[15]);
  not not_3 (not_3_out, xor_1_out);
  not not_4 (not_4_out, A[15]);
  xor xor_2 (xor_2_out, Result[0], B[15]);
  and and_1 (and_1_out, not_3_out, Negative_Bit, not_4_out);
  and and_2 (and_2_out, xor_2_out, not_2_out, A[15]);
  or or_2 (Overflow_Bit, and_1_out, and_2_out);

  assign Result[15] = Negative_Bit;

  // Notes on the sheet:
  //   16-Bit Adder
  //   Please notice that you need to generate the four flag bits for the adder.
endmodule

module _16_Bit_Subtractor (
  input  [15:0] A,
  input  [15:0] B,
  output [15:0] Result,
  output Carry_Out,
  output Negative_Bit,
  output Zero_Bit,
  output Overflow_Bit
);

  wire and_1_out, and_2_out, not_2_out, not_3_out, not_4_out, or_1_out, xor_1_out, xor_2_out;

  Subtractor #(.width(16)) subtractor_1 (
    .a(A), .b(B), .out({Negative_Bit, Result[14:0]}), .bin(1'b0), .bout(Carry_Out));
  or or_1 (or_1_out, Negative_Bit, Result[14], Result[13], Result[12], Result[11], Result[10], Result[9], Result[8], Result[6], Result[5], Result[4], Result[3], Result[2], Result[1], Result[0], Result[7]);
  not not_1 (Zero_Bit, or_1_out);
  not not_2 (not_2_out, Negative_Bit);
  xor xor_1 (xor_1_out, Result[0], B[15]);
  not not_3 (not_3_out, xor_1_out);
  not not_4 (not_4_out, A[15]);
  xor xor_2 (xor_2_out, Result[0], B[15]);
  and and_1 (and_1_out, not_3_out, Negative_Bit, not_4_out);
  and and_2 (and_2_out, xor_2_out, not_2_out, A[15]);
  or or_2 (Overflow_Bit, and_1_out, and_2_out);

  assign Result[15] = Negative_Bit;

  // Notes on the sheet:
  //   16-Bit Subtractor
  //   Please notice that you need to generate the four flag bits for the subtractor
endmodule

module _16_Bit_Left_Shifter_Circuit (
  input  [15:0] in_1,
  input  [15:0] in_2,
  output [15:0] out_3
);

  wire [3:0] bit_extender_1_out;

  Bit_Extender #(.in_width(16), .out_width(4)) bit_extender_1 (.in(in_2), .out(bit_extender_1_out));
  Shifter #(.width(16)) shifter_1 (.in(in_1), .\dist (bit_extender_1_out), .out(out_3));

  // Notes on the sheet:
  //   16-Bit Left Shifter Circuit
  //   Shift A to left by B bits
endmodule

module _16_Bit_Right_Shfit_Circuit (
  input  [15:0] in_1,
  input  [15:0] in_2,
  output [15:0] out_3
);

  wire [3:0] bit_extender_1_out;

  Bit_Extender #(.in_width(16), .out_width(4)) bit_extender_1 (.in(in_2), .out(bit_extender_1_out));
  Shifter #(.width(16), .shift("ar")) shifter_1 (.in(in_1), .\dist (bit_extender_1_out), .out(out_3));

  // Notes on the sheet:
  //   16-Bit Right Shifter Circuit
  //   Shift A to Right by B bits
endmodule

module Main_ALU_Circuit (
  input  [15:0] in_1,
  input  [15:0] in_2,
  input  in_3,
  input  [2:0] in_4,
  output [3:0] out_5,
  output [15:0] out_6
);

  wire [3:0] n16_bit_adder_1_overflow_bit, n16_bit_subtractor_1_overflow_bit;
  wire [15:0] n16_bit_adder_1_result, n16_bit_and_1_out_3, n16_bit_inverter_1_result,
       n16_bit_left_shifter_circuit_1_out_3, n16_bit_or_1_result, n16_bit_right_shfit_circuit_1_out_3,
       n16_bit_subtractor_1_result, n16_bit_xor_1_result;

  _16_Bit_AND u_16_bit_and_1 (.A(in_1), .B(in_2), .out_3(n16_bit_and_1_out_3));
  _16_Bit_OR u_16_bit_or_1 (.A(in_1), .B(in_2), .Result(n16_bit_or_1_result));
  _16_Bit_XOR u_16_bit_xor_1 (.A(in_1), .B(in_2), .Result(n16_bit_xor_1_result));
  _16_Bit_Inverter u_16_bit_inverter_1 (.A(in_1), .Result(n16_bit_inverter_1_result));
  _16_Bit_Right_Shfit_Circuit u_16_bit_right_shfit_circuit_1 (
    .in_1(in_1), .in_2(in_2), .out_3(n16_bit_right_shfit_circuit_1_out_3));
  _16_Bit_Left_Shifter_Circuit u_16_bit_left_shifter_circuit_1 (
    .in_1(in_1), .in_2(in_2), .out_3(n16_bit_left_shifter_circuit_1_out_3));
  _16_Bit_Adder u_16_bit_adder_1 (
    .A(in_1), .B(in_2), .Carry_Out(n16_bit_adder_1_overflow_bit[3]),
    .Negative_Bit(n16_bit_adder_1_overflow_bit[2]), .Zero_Bit(n16_bit_adder_1_overflow_bit[1]),
    .Result(n16_bit_adder_1_result), .Overflow_Bit(n16_bit_adder_1_overflow_bit[0]));
  _16_Bit_Subtractor u_16_bit_subtractor_1 (
    .A(in_1), .B(in_2), .Carry_Out(n16_bit_subtractor_1_overflow_bit[3]),
    .Negative_Bit(n16_bit_subtractor_1_overflow_bit[2]), .Zero_Bit(n16_bit_subtractor_1_overflow_bit[1]),
    .Result(n16_bit_subtractor_1_result), .Overflow_Bit(n16_bit_subtractor_1_overflow_bit[0]));
  Multiplexer #(.select(3), .width(16)) multiplexer_1 (
    .in0(n16_bit_adder_1_result), .in1(n16_bit_subtractor_1_result), .in2(n16_bit_and_1_out_3),
    .in3(n16_bit_or_1_result), .in4(n16_bit_xor_1_result), .in5(n16_bit_inverter_1_result),
    .in6(n16_bit_right_shfit_circuit_1_out_3), .in7(n16_bit_left_shifter_circuit_1_out_3), .out(out_6),
    .sel(in_4));  // open: en
  Multiplexer #(.width(4)) multiplexer_2 (
    .in0(n16_bit_adder_1_overflow_bit), .in1(n16_bit_subtractor_1_overflow_bit), .out(out_5), .sel(in_3));  // open: en

  // Notes on the sheet:
  //   Main ALU Circuit to Build
  //   Needs to use all the subcircuits you built
endmodule
